// Logisim project MCU.circ as structural Verilog
module MCU (
  input  [4:0] KBD_command,
  input  [10:0] KBD_energy_increment,
  input  KBD_Ready,
  input  MISO,
  input  SPI_busy,
  input  CLK,
  input  Reset,
  output Request_KBD_command,
  output Request_KBD_energy,
  output [7:0] Cell_CSC,
  output [7:0] Cell_CSR,
  output [2:0] Table_CSC,
  output SPI_clock,
  output [5:0] Table_CSR,
  output MOSI,
  output Task_CS,
  output Waiting_IO,
  output SPI_communication_in_progress
);
endmodule
